# Fritzing sketch DC_Motor_power_circuit (saved by Fritzing 0.9.4)
circuit board: 6.88566cm x 5.36311cm
breadboards: 2

parts:
  Motor = DC Motor
  Battery = Battery block 9V
  FET = Basic FET N-Channel [package="TO220 [THT]"]
  Arduino1 = Arduino Uno (Rev3)

nets:
  N1: Motor.pin_1, FET.drain
  N2: Motor.pin_2, Battery.+
  N3: Battery.-, FET.source, Arduino1.GND
  N4: FET.gate, Arduino1.D9_PWM

notes:
  +
  -
  AMPLIFIER
